// Logisim project priya.circ as structural Verilog: 1 circuit, main circuit main
module main (
  input  in_1,
  input  in_2,
  output out_3
);

  wire and_1_out, and_2_out, not_1_out, not_2_out, or_1_out;
  wire [1:0] undriven_3, xor_1_out;
  wire [1:1] undriven, undriven_2, xor_2_out;

  assign xor_1_out = {undriven[1], in_1} ^ {undriven_2[1], in_2};  // XOR_Gate xor_1, 2 bits wide
  not not_1 (not_1_out, in_1);
  and and_1 (and_1_out, not_1_out, in_2);
  not not_2 (not_2_out, xor_1_out[0]);
  assign {xor_2_out[1], out_3} = undriven_3 ^ xor_1_out;  // XOR_Gate xor_2, 2 bits wide
  and and_2 (and_2_out, not_2_out, undriven_3[0]);
  or or_1 (or_1_out, and_2_out, and_1_out);
  // Pins of 1 and 2 bits meet at xor_1_out
  // Pins of 1 and 2 bits meet at {undriven[1], in_1}
  // Pins of 1 and 2 bits meet at {undriven_2[1], in_2}
  // Pins of 1 and 2 bits meet at undriven_3
  // Pins of 1 and 2 bits meet at {xor_2_out[1], out_3}
endmodule
